# Fritzing sketch CIRC11-MIB (saved by Fritzing 0.9.3b)
breadboards: 1

parts:
  Part2 = Adafruit Metro with Headers [part_number="Adafruit #2488"]
  R1 = Relay 5v DPDT  # not connected
  D1 = Rectifier Diode [part_number=1N4001 package="300 mil [THT]"]
  R2 = Resistor [tolerance=±5% resistance=2.2k package=THT]
  Q2 = NPN-Transistor [package="TO92 [THT]"]
  M1 = DC Motor

nets:
  N1: Part2.IO2, R2.Pin_0
  N2: Part2.+5V, D1.cathode, M1.pin_2
  N3: Part2.GND, Q2.C, M1.pin_1
  N4: R2.Pin_1, Q2.B

custom parts:
  Adafruit Metro with Headers: We sure love the ATmega328 here at Adafruit, and we use them a lot for our own projects. The processor has plenty of GPIO, Analog inputs, hardware UART SPI and I2C, timers and PWM galore - just enough for most simple projects. When we need to go small, we use a Pro Trinket 3V or 5V, but when size isn't as much of a concern, and an USB-serial converter is required, we reach for an Adafruit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
  Relay 5v DPDT: 5v DPDT Relay, 8 pin
