# Fritzing sketch CIRC14-LCD (saved by Fritzing 0.9.3b)
breadboards: 1

parts:
  U2 = LCD-16X2 [package=lcd-16x2_noholes]
  Part3 = Adafruit Metro M0 Express
  POT1 = Breadboard Trimpot

nets:
  VSS: U2.VSS, U2.R_W, U2.K, Part3.GND, POT1.PIN3
  VDD: U2.VDD, U2.A, Part3.+5V, POT1.PIN1
  N1: U2.VO, POT1.PIN2
  N2: U2.RS, Part3.D7
  N3: U2.E, Part3.D8
  N4: U2.DB4, Part3.D9
  N5: U2.DB5, Part3.D10
  N6: U2.DB6, Part3.D11
  N7: U2.DB7, Part3.D12

custom parts:
  Adafruit Metro M0 Express: Metro is our series of microcontroller boards for use with the Arduino IDE. This new Metro board looks a whole lot like our original Metro 328, but with a huge upgrade. Instead of the ATmega328, this Metro features a ATSAMD21G18 chip, an ARM Cortex M0+. It's our first Metro that is designed for use with CircuitPython! CircuitPython is our beginner-oriented flavor of MicroPython - and as the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
