# Fritzing sketch CIRC15-RGB (saved by Fritzing 0.9.3b)
breadboards: 1

parts:
  R1 = Resistor [tolerance=±5% resistance=560 package=THT]
  R2 = Resistor [tolerance=±5% resistance=560 package=THT]
  R3 = Resistor [tolerance=±5% resistance=560 package=THT]
  IR1 = TSOP312.., 314.. [package=THT]
  LED1 = RGB LED - (4 legs) [package="5 mm [THT]"]
  Part4 = Adafruit Metro with Headers [part_number="Adafruit #2488"]

nets:
  N1: R1.Pin_0, Part4.SS
  N2: R1.Pin_1, LED1.green_cathode
  N3: R2.Pin_0, Part4.IO9
  N4: R2.Pin_1, LED1.red_cathode
  N5: R3.Pin_0, Part4.MOSI
  N6: R3.Pin_1, LED1.blue_cathode
  N7: IR1.GND, Part4.IO6
  N8: IR1.Vs, Part4.GND
  N9: LED1.common_anode, Part4.3.3V

custom parts:
  Adafruit Metro with Headers: We sure love the ATmega328 here at Adafruit, and we use them a lot for our own projects. The processor has plenty of GPIO, Analog inputs, hardware UART SPI and I2C, timers and PWM galore - just enough for most simple projects. When we need to go small, we use a Pro Trinket 3V or 5V, but when size isn't as much of a concern, and an USB-serial converter is required, we reach for an Adafruit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
