# Fritzing sketch CIRC15 (saved by Fritzing 0.9.3b)
breadboards: 1

parts:
  IR1 = TSOP312.., 314.. [package=THT]
  LED1 = LED - 5mm [color="Red (633nm)" package="5 mm [THT]"]
  R1 = Resistor [tolerance=±5% resistance=560 package=THT]
  Part4 = Adafruit Metro with Headers [part_number="Adafruit #2488"]

nets:
  N1: IR1.GND, Part4.IO6
  N2: IR1.Vs, R1.Pin_0, Part4.GND
  N3: IR1.Data, Part4.+5V
  N4: LED1.cathode, R1.Pin_1
  N5: LED1.anode, Part4.MOSI

custom parts:
  Adafruit Metro with Headers: We sure love the ATmega328 here at Adafruit, and we use them a lot for our own projects. The processor has plenty of GPIO, Analog inputs, hardware UART SPI and I2C, timers and PWM galore - just enough for most simple projects. When we need to go small, we use a Pro Trinket 3V or 5V, but when size isn't as much of a concern, and an USB-serial converter is required, we reach for an Adafruit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
