# Fritzing sketch CIRC16 (saved by Fritzing 0.9.3b)
breadboards: 1

parts:
  Part2 = Adafruit Metro with Headers [part_number="Adafruit #2488"]
  IR1 = TSOP312.., 314.. [package=THT]
  LED1 = Infrared LED - 5mm [package="5 mm [THT]"]  # not connected
  Q1 = NPN-Transistor [package="TO92 [THT]"]
  R1 = Resistor [tolerance=±5% resistance=560 package=THT]
  LED2 = LED - 5mm [color="Red (633nm)" package="5 mm [THT]"]
  R2 = Resistor [tolerance=±5% resistance=560 package=THT]
  S1 = Pushbutton [package="[THT]"]
  S2 = Pushbutton [package="[THT]"]
  R3 = Resistor [tolerance=±5% resistance=10k package=THT]
  R4 = Resistor [tolerance=±5% resistance=10k package=THT]

nets:
  N1: Part2.SCK, S1.Pin_3, S1.Pin_4, R3.Pin_1
  N2: Part2.MOSI, S2.Pin_3, S2.Pin_4, R4.Pin_1
  N3: Part2.IO9, R1.Pin_0
  N4: Part2.IO4, LED2.anode
  N5: Part2.IO3, IR1.GND
  N6: Part2.3.3V, IR1.Data, S1.Pin_1, S1.Pin_2, S2.Pin_1, S2.Pin_2, R3.Pin_0, R4.Pin_0
  N7: Part2.GND, IR1.Vs, Q1.E, R2.Pin_0
  N8: Q1.B, R1.Pin_1
  N9: LED2.cathode, R2.Pin_1

notes:
  REC
  PLAY

custom parts:
  Adafruit Metro with Headers: We sure love the ATmega328 here at Adafruit, and we use them a lot for our own projects. The processor has plenty of GPIO, Analog inputs, hardware UART SPI and I2C, timers and PWM galore - just enough for most simple projects. When we need to go small, we use a Pro Trinket 3V or 5V, but when size isn't as much of a concern, and an USB-serial converter is required, we reach for an Adafruit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
  Infrared LED - 5mm: A generic infrared LED (~1.2V)
