# Fritzing sketch PROJ01 (saved by Fritzing 0.9.3b)
breadboards: 1

parts:
  J1 = Piezo Speaker
  Q1 = LTR-301 [package=ltr-301]
  R1 = Resistor [tolerance=±5% resistance=560 package=THT]
  Part4 = Adafruit Metro with Headers [part_number="Adafruit #2488"]

nets:
  N1: J1.pin1, Q1.C, Part4.GND
  N2: J1.pin2, Part4.IO9
  N3: Q1.E, R1.Pin_1, Part4.AD0
  N4: R1.Pin_0, Part4.+5V

custom parts:
  Adafruit Metro with Headers: We sure love the ATmega328 here at Adafruit, and we use them a lot for our own projects. The processor has plenty of GPIO, Analog inputs, hardware UART SPI and I2C, timers and PWM galore - just enough for most simple projects. When we need to go small, we use a Pro Trinket 3V or 5V, but when size isn't as much of a concern, and an USB-serial converter is required, we reach for an Adafruit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
