# Fritzing sketch PROJ02 (saved by Fritzing 0.9.3b)
breadboards: 1

parts:
  Part1 = Adafruit Metro with Headers [part_number="Adafruit #2488"]
  LED24 = LED - 5mm [color="Green (555nm)" package="5 mm [THT]"]
  LED17 = LED - 5mm [color="Green (555nm)" package="5 mm [THT]"]
  LED18 = LED - 5mm [color="Green (555nm)" package="5 mm [THT]"]
  LED19 = LED - 5mm [color="Green (555nm)" package="5 mm [THT]"]
  LED20 = LED - 5mm [color="Green (555nm)" package="5 mm [THT]"]
  LED21 = LED - 5mm [color="Green (555nm)" package="5 mm [THT]"]
  LED22 = LED - 5mm [color="Green (555nm)" package="5 mm [THT]"]
  LED23 = LED - 5mm [color="Green (555nm)" package="5 mm [THT]"]
  R19 = Resistor [tolerance=±5% resistance=560 package=THT]
  R20 = Resistor [tolerance=±5% resistance=560 package=THT]
  R21 = Resistor [tolerance=±5% resistance=560 package=THT]
  R22 = Resistor [tolerance=±5% resistance=560 package=THT]
  R23 = Resistor [tolerance=±5% resistance=560 package=THT]
  R24 = Resistor [tolerance=±5% resistance=560 package=THT]
  R25 = Resistor [tolerance=±5% resistance=560 package=THT]
  R26 = Resistor [tolerance=±5% resistance=560 package=THT]
  VCC1 = Battery block 9V  # not connected
  JACK1 = 2.1mm DC Barrel Jack  # not connected

nets:
  N1: Part1.IO9, LED17.anode
  N2: Part1.IO8, LED19.anode
  N3: Part1.IO7, LED20.anode
  N4: Part1.IO6, LED22.anode
  N5: Part1.IO5, LED23.anode
  N6: Part1.IO4, LED24.anode
  N7: Part1.IO3, LED18.anode
  N8: Part1.IO2, LED21.anode
  N9: Part1.GND, R19.Pin_1, R20.Pin_1, R21.Pin_1, R22.Pin_1, R23.Pin_1, R24.Pin_1, R25.Pin_1, R26.Pin_1
  N10: LED24.cathode, R24.Pin_0
  N11: LED17.cathode, R19.Pin_0
  N12: LED18.cathode, R25.Pin_0
  N13: LED19.cathode, R20.Pin_0
  N14: LED20.cathode, R21.Pin_0
  N15: LED21.cathode, R26.Pin_0
  N16: LED22.cathode, R22.Pin_0
  N17: LED23.cathode, R23.Pin_0

custom parts:
  Adafruit Metro with Headers: We sure love the ATmega328 here at Adafruit, and we use them a lot for our own projects. The processor has plenty of GPIO, Analog inputs, hardware UART SPI and I2C, timers and PWM galore - just enough for most simple projects. When we need to go small, we use a Pro Trinket 3V or 5V, but when size isn't as much of a concern, and an USB-serial converter is required, we reach for an Adafruit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
  2.1mm DC Barrel Jack: 2.1mm DC Barrel Jack with Thru-Hole Connectors (breadboardable)
