# Fritzing sketch PROJ03 (saved by Fritzing 0.9.3b)
breadboards: 1

parts:
  Part2 = Adafruit Metro with Headers [part_number="Adafruit #2488"]
  U1 = LCD-16X2 [package=lcd-16x2_noholes]
  POT1 = Breadboard Trimpot
  Q1 = LTR-301 [package=ltr-301]
  R1 = Resistor [tolerance=±5% resistance=10k package=THT]
  J1 = Piezo Speaker

nets:
  N1: Part2.AD0, Q1.E, R1.Pin_1
  N2: Part2.SCK, J1.pin2
  N3: Part2.MISO, U1.DB7
  N4: Part2.MOSI, U1.DB6
  N5: Part2.SS, U1.DB5
  N6: Part2.IO9, U1.DB4
  N7: Part2.IO8, U1.E
  N8: Part2.IO7, U1.RS
  +5V: Part2.+5V, U1.VDD, U1.A, POT1.PIN3, R1.Pin_0
  GND: Part2.GND, U1.VSS, U1.R_W, U1.K, POT1.PIN1, Q1.C, J1.pin1
  N9: U1.VO, POT1.PIN2

custom parts:
  Adafruit Metro with Headers: We sure love the ATmega328 here at Adafruit, and we use them a lot for our own projects. The processor has plenty of GPIO, Analog inputs, hardware UART SPI and I2C, timers and PWM galore - just enough for most simple projects. When we need to go small, we use a Pro Trinket 3V or 5V, but when size isn't as much of a concern, and an USB-serial converter is required, we reach for an Adafruit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
