# Fritzing sketch PROJ06 (saved by Fritzing 0.9.3b)
breadboards: 1

parts:
  IR1 = TSOP312.., 314.. [package=THT]
  Part4 = Adafruit Metro M0 Express
  SERVO1 = Tower Pro SG90 servo [part_number=101246]  # not connected
  LD1 = LD  # not connected

nets:
  GND: IR1.GND, Part4.GND
  N1: IR1.Vs, Part4.D2
  N2: IR1.Data, Part4.+5V

custom parts:
  Adafruit Metro M0 Express: Metro is our series of microcontroller boards for use with the Arduino IDE. This new Metro board looks a whole lot like our original Metro 328, but with a huge upgrade. Instead of the ATmega328, this Metro features a ATSAMD21G18 chip, an ARM Cortex M0+. It's our first Metro that is designed for use with CircuitPython! CircuitPython is our beginner-oriented flavor of MicroPython - and as the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
  Tower Pro SG90 servo: Original file by John De Cristofaro http://www.adafruit.com/products/1449 Adafruit Feedback Servo (Small) Edited by: e-radionica.com 28/9/2015
  LD: A Generic Red Dot Laser Diode Module (~5mW)
