# Fritzing sketch circ02 (saved by Fritzing 0.9.3b)
breadboards: 1

parts:
  Part1 = Adafruit Metro with Headers [part_number="Adafruit #2488"]
  R1 = Resistor [tolerance=±5% resistance=560 package=THT]
  R2 = Resistor [tolerance=±5% resistance=560 package=THT]
  R4 = Resistor [tolerance=±5% resistance=560 package=THT]
  R5 = Resistor [tolerance=±5% resistance=560 package=THT]
  R6 = Resistor [tolerance=±5% resistance=560 package=THT]
  R8 = Resistor [tolerance=±5% resistance=560 package=THT]
  LED9 = LED - 5mm [color="Green (555nm)" package="5 mm [THT]"]
  LED10 = LED - 5mm [color="Green (555nm)" package="5 mm [THT]"]
  LED11 = LED - 5mm [color="Green (555nm)" package="5 mm [THT]"]
  LED12 = LED - 5mm [color="Green (555nm)" package="5 mm [THT]"]
  LED13 = LED - 5mm [color="Green (555nm)" package="5 mm [THT]"]
  LED14 = LED - 5mm [color="Green (555nm)" package="5 mm [THT]"]
  LED15 = LED - 5mm [color="Green (555nm)" package="5 mm [THT]"]
  LED16 = LED - 5mm [color="Green (555nm)" package="5 mm [THT]"]
  R9 = Resistor [tolerance=±5% resistance=560 package=THT]
  R11 = Resistor [tolerance=±5% resistance=560 package=THT]

nets:
  N1: Part1.IO9, LED9.anode
  N2: Part1.IO8, LED10.anode
  N3: Part1.IO7, LED11.anode
  N4: Part1.IO6, LED12.anode
  N5: Part1.IO5, LED13.anode
  N6: Part1.IO4, LED14.anode
  N7: Part1.IO3, LED15.anode
  N8: Part1.IO2, LED16.anode
  N9: Part1.GND, R1.Pin_1, R2.Pin_1, R4.Pin_1, R5.Pin_1, R6.Pin_1, R8.Pin_1, R9.Pin_1, R11.Pin_1
  N10: R1.Pin_0, LED9.cathode
  N11: R2.Pin_0, LED10.cathode
  N12: R4.Pin_0, LED11.cathode
  N13: R5.Pin_0, LED12.cathode
  N14: R6.Pin_0, LED13.cathode
  N15: R8.Pin_0, LED15.cathode
  N16: LED14.cathode, R11.Pin_0
  N17: LED16.cathode, R9.Pin_0

custom parts:
  Adafruit Metro with Headers: We sure love the ATmega328 here at Adafruit, and we use them a lot for our own projects. The processor has plenty of GPIO, Analog inputs, hardware UART SPI and I2C, timers and PWM galore - just enough for most simple projects. When we need to go small, we use a Pro Trinket 3V or 5V, but when size isn't as much of a concern, and an USB-serial converter is required, we reach for an Adafruit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
