# Fritzing sketch circ03 (saved by Fritzing 0.9.3b)
breadboards: 1

parts:
  Part2 = Adafruit Metro with Headers [part_number="Adafruit #2488"]
  M1 = DC Motor
  Q1 = NPN-Transistor [package="SOT-23 [SMD]"]
  D2 = P1000K [part_number=P1000K]
  R1 = Resistor [tolerance=±5% resistance=2.2k package="2512 [SMD]"]

nets:
  N1: Part2.IO9, R1.Pin_0
  N2: Part2.+5V, M1.pin_1, D2.cathode
  N3: Part2.GND, Q1.2
  N4: M1.pin_2, Q1.1, D2.anode
  N5: Q1.0, R1.Pin_1

notes:
  Emitter
  Base
  Collector
  -
  +

custom parts:
  Adafruit Metro with Headers: We sure love the ATmega328 here at Adafruit, and we use them a lot for our own projects. The processor has plenty of GPIO, Analog inputs, hardware UART SPI and I2C, timers and PWM galore - just enough for most simple projects. When we need to go small, we use a Pro Trinket 3V or 5V, but when size isn't as much of a concern, and an USB-serial converter is required, we reach for an Adafruit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
