# Fritzing sketch circ05 (saved by Fritzing 0.9.3b)
breadboards: 1

parts:
  Part2 = Adafruit Metro with Headers [part_number="Adafruit #2488"]
  U1 = 74HC595 [package="DIP16 [THT]"]
  LED1 = LED Red 3mm - Top View [package="3 mm [THT] Top View"]
  LED2 = LED Red 3mm - Top View [package="3 mm [THT] Top View"]
  LED3 = LED Red 3mm - Top View [package="3 mm [THT] Top View"]
  LED4 = LED Red 3mm - Top View [package="3 mm [THT] Top View"]
  LED5 = LED Red 3mm - Top View [package="3 mm [THT] Top View"]
  LED6 = LED Red 3mm - Top View [package="3 mm [THT] Top View"]
  LED7 = LED Red 3mm - Top View [package="3 mm [THT] Top View"]
  LED8 = LED Red 3mm - Top View [package="3 mm [THT] Top View"]
  R1 = Resistor [tolerance=±5% resistance=560 package=THT]
  R2 = Resistor [tolerance=±5% resistance=560 package=THT]
  R3 = Resistor [tolerance=±5% resistance=560 package=THT]
  R4 = Resistor [tolerance=±5% resistance=560 package=THT]
  R5 = Resistor [tolerance=±5% resistance=560 package=THT]
  R6 = Resistor [tolerance=±5% resistance=560 package=THT]
  R7 = Resistor [tolerance=±5% resistance=560 package=THT]
  R8 = Resistor [tolerance=±5% resistance=560 package=THT]

nets:
  N1: Part2.IO4, U1.ST_CP
  N2: Part2.IO3, U1.SH_CP
  N3: Part2.IO2, U1.DS
  +5V: Part2.+5V, U1.MR, U1.VCC
  GND: Part2.GND, U1.GND, U1.OE, R1.Pin_1, R2.Pin_1, R3.Pin_1, R4.Pin_1, R5.Pin_1, R6.Pin_1, R7.Pin_1, R8.Pin_1
  N4: U1.Q1, LED2.anode
  N5: U1.Q2, LED3.anode
  N6: U1.Q3, LED4.anode
  N7: U1.Q4, LED5.anode
  N8: U1.Q5, LED6.anode
  N9: U1.Q6, LED7.anode
  N10: U1.Q7, LED8.anode
  N11: U1.Q0, LED1.anode
  N12: LED1.cathode, R5.Pin_0
  N13: LED2.cathode, R6.Pin_0
  N14: LED3.cathode, R7.Pin_0
  N15: LED4.cathode, R8.Pin_0
  N16: LED5.cathode, R1.Pin_0
  N17: LED6.cathode, R2.Pin_0
  N18: LED7.cathode, R3.Pin_0
  N19: LED8.cathode, R4.Pin_0

custom parts:
  Adafruit Metro with Headers: We sure love the ATmega328 here at Adafruit, and we use them a lot for our own projects. The processor has plenty of GPIO, Analog inputs, hardware UART SPI and I2C, timers and PWM galore - just enough for most simple projects. When we need to go small, we use a Pro Trinket 3V or 5V, but when size isn't as much of a concern, and an USB-serial converter is required, we reach for an Adafruit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
  LED Red 3mm - Top View: A generic red LED (~1.8V)
