# Fritzing sketch circ09-servo (saved by Fritzing 0.9.3b)
breadboards: 1

parts:
  Part2 = Adafruit Metro with Headers [part_number="Adafruit #2488"]
  R3 = Resistor [tolerance=±5% resistance=10k package=THT]
  Q1 = LTR-301 [package=ltr-301]
  SERVO1 = Tower Pro SG90 servo [part_number=101246]

nets:
  N1: Part2.AD0, R3.Pin_1, Q1.E
  N2: Part2.IO9, SERVO1.Signal
  +5V: Part2.+5V, R3.Pin_0, SERVO1.+5V
  GND: Part2.GND, Q1.C, SERVO1.GND

custom parts:
  Adafruit Metro with Headers: We sure love the ATmega328 here at Adafruit, and we use them a lot for our own projects. The processor has plenty of GPIO, Analog inputs, hardware UART SPI and I2C, timers and PWM galore - just enough for most simple projects. When we need to go small, we use a Pro Trinket 3V or 5V, but when size isn't as much of a concern, and an USB-serial converter is required, we reach for an Adafruit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
  Tower Pro SG90 servo: Original file by John De Cristofaro http://www.adafruit.com/products/1449 Adafruit Feedback Servo (Small) Edited by: e-radionica.com 28/9/2015
