# Fritzing sketch circ10 (saved by Fritzing 0.9.3b)
breadboards: 1

parts:
  U1 = TMP36 [package=to-92]
  BAT1 = BC9VPC [package=bc9vpc]
  JACK1 = 2.1mm DC Barrel Jack
  J1 = Piezo Speaker
  Part4 = Adafruit Metro with Headers [part_number="Adafruit #2488"]

nets:
  VCC: U1.VCC, Part4.3.3V
  N1: U1.VOUT, Part4.AD0
  GND: U1.GND, J1.pin1, Part4.GND
  N2: BAT1.V+, JACK1.center
  N3: BAT1.V-, JACK1.sleeve
  N4: J1.pin2, Part4.IO9

custom parts:
  2.1mm DC Barrel Jack: 2.1mm DC Barrel Jack with Thru-Hole Connectors (breadboardable)
  Adafruit Metro with Headers: We sure love the ATmega328 here at Adafruit, and we use them a lot for our own projects. The processor has plenty of GPIO, Analog inputs, hardware UART SPI and I2C, timers and PWM galore - just enough for most simple projects. When we need to go small, we use a Pro Trinket 3V or 5V, but when size isn't as much of a concern, and an USB-serial converter is required, we reach for an Adafruit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
