# Fritzing sketch CIRC01-express (saved by Fritzing 0.9.3b)
breadboards: 1

parts:
  LED2 = LEDs [package=led10mm]
  R1 = Resistor [tolerance=±5% resistance=560 package=THT]
  Part2 = Adafruit Metro M0 Express

nets:
  N1: LED2.C, R1.Pin_0
  N2: LED2.A, Part2.D13
  N3: R1.Pin_1, Part2.GND

custom parts:
  Adafruit Metro M0 Express: Metro is our series of microcontroller boards for use with the Arduino IDE. This new Metro board looks a whole lot like our original Metro 328, but with a huge upgrade. Instead of the ATmega328, this Metro features a ATSAMD21G18 chip, an ARM Cortex M0+. It's our first Metro that is designed for use with CircuitPython! CircuitPython is our beginner-oriented flavor of MicroPython - and as the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
