# Fritzing sketch CIRC04-express (saved by Fritzing 0.9.3b)
breadboards: 1

parts:
  J1 = Dagu DGServo 9g header connector (female) [package=THT]
  M1 = Dagu DGServo 9g (Top view) [part_number=RS001B]  # not connected
  Part3 = Adafruit Metro M0 Express

nets:
  GND: J1.gnd, Part3.GND
  VCC: J1.Vcc, Part3.3.3V
  N1: J1.pulse, Part3.D9

custom parts:
  Adafruit Metro M0 Express: Metro is our series of microcontroller boards for use with the Arduino IDE. This new Metro board looks a whole lot like our original Metro 328, but with a huge upgrade. Instead of the ATmega328, this Metro features a ATSAMD21G18 chip, an ARM Cortex M0+. It's our first Metro that is designed for use with CircuitPython! CircuitPython is our beginner-oriented flavor of MicroPython - and as the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
