# Fritzing sketch CIRC05-express (saved by Fritzing 0.9.3b)
breadboards: 1

parts:
  U1 = 74HC595 [package="DIP16 [THT]"]
  LED1 = LED Red 3mm - Top View [package="3 mm [THT] Top View"]
  LED2 = LED Red 3mm - Top View [package="3 mm [THT] Top View"]
  LED3 = LED Red 3mm - Top View [package="3 mm [THT] Top View"]
  LED4 = LED Red 3mm - Top View [package="3 mm [THT] Top View"]
  LED5 = LED Red 3mm - Top View [package="3 mm [THT] Top View"]
  LED6 = LED Red 3mm - Top View [package="3 mm [THT] Top View"]
  LED7 = LED Red 3mm - Top View [package="3 mm [THT] Top View"]
  LED8 = LED Red 3mm - Top View [package="3 mm [THT] Top View"]
  R1 = Resistor [tolerance=±5% resistance=560 package=THT]
  R2 = Resistor [tolerance=±5% resistance=560 package=THT]
  R3 = Resistor [tolerance=±5% resistance=560 package=THT]
  R4 = Resistor [tolerance=±5% resistance=560 package=THT]
  R5 = Resistor [tolerance=±5% resistance=560 package=THT]
  R6 = Resistor [tolerance=±5% resistance=560 package=THT]
  R7 = Resistor [tolerance=±5% resistance=560 package=THT]
  R8 = Resistor [tolerance=±5% resistance=560 package=THT]
  Part3 = Adafruit Metro M0 Express

nets:
  N1: U1.Q1, LED2.anode
  N2: U1.Q2, LED3.anode
  N3: U1.Q3, LED4.anode
  N4: U1.Q4, LED5.anode
  N5: U1.Q5, LED6.anode
  N6: U1.Q6, LED7.anode
  N7: U1.Q7, LED8.anode
  GND: U1.GND, U1.OE, R1.Pin_1, R2.Pin_1, R3.Pin_1, R4.Pin_1, R5.Pin_1, R6.Pin_1, R7.Pin_1, R8.Pin_1, Part3.GND
  VCC: U1.MR, U1.VCC, Part3.3.3V
  N8: U1.SH_CP, Part3.D3
  N9: U1.ST_CP, Part3.D4
  N10: U1.DS, Part3.D2
  N11: U1.Q0, LED1.anode
  N12: LED1.cathode, R5.Pin_0
  N13: LED2.cathode, R6.Pin_0
  N14: LED3.cathode, R7.Pin_0
  N15: LED4.cathode, R8.Pin_0
  N16: LED5.cathode, R1.Pin_0
  N17: LED6.cathode, R2.Pin_0
  N18: LED7.cathode, R3.Pin_0
  N19: LED8.cathode, R4.Pin_0

custom parts:
  LED Red 3mm - Top View: A generic red LED (~1.8V)
  Adafruit Metro M0 Express: Metro is our series of microcontroller boards for use with the Arduino IDE. This new Metro board looks a whole lot like our original Metro 328, but with a huge upgrade. Instead of the ATmega328, this Metro features a ATSAMD21G18 chip, an ARM Cortex M0+. It's our first Metro that is designed for use with CircuitPython! CircuitPython is our beginner-oriented flavor of MicroPython - and as the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
