# Fritzing sketch CIRC10-express-alarm (saved by Fritzing 0.9.3b)
breadboards: 1

parts:
  U1 = TMP36 [package=to-92]
  Part3 = Adafruit Metro M0 Express
  BAT1 = BC9VPC [package=bc9vpc]
  JACK1 = 2.1mm DC Barrel Jack
  J1 = Piezo Speaker

nets:
  VCC: U1.VCC, Part3.3.3V
  N1: U1.VOUT, Part3.A0
  GND: U1.GND, Part3.GND, J1.pin1
  N2: Part3.D8, J1.pin2
  N3: BAT1.V+, JACK1.center
  N4: BAT1.V-, JACK1.sleeve

custom parts:
  Adafruit Metro M0 Express: Metro is our series of microcontroller boards for use with the Arduino IDE. This new Metro board looks a whole lot like our original Metro 328, but with a huge upgrade. Instead of the ATmega328, this Metro features a ATSAMD21G18 chip, an ARM Cortex M0+. It's our first Metro that is designed for use with CircuitPython! CircuitPython is our beginner-oriented flavor of MicroPython - and as the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
  2.1mm DC Barrel Jack: 2.1mm DC Barrel Jack with Thru-Hole Connectors (breadboardable)
