# Fritzing sketch CIRC11-express (saved by Fritzing 0.9.3b)
breadboards: 1

parts:
  R1 = Relay 5v DPDT  # not connected
  D1 = Rectifier Diode [part_number=1N4001 package="300 mil [THT]"]
  R2 = Resistor [tolerance=±5% resistance=2.2k package=THT]
  LED1 = LED - 5mm [color="Green (565nm)" package="5 mm [THT]"]
  LED2 = LED - 5mm [color="Red (633nm)" package="5 mm [THT]"]
  R3 = Resistor [tolerance=±5% resistance=560 package=THT]
  R4 = Resistor [tolerance=±5% resistance=560 package=THT]
  Q2 = NPN-Transistor [package="TO92 [THT]"]
  Part3 = Adafruit Metro M0 Express

nets:
  N1: D1.cathode, Part3.3.3V
  N2: D1.anode, Q2.E
  N3: R2.Pin_0, Part3.D2
  N4: R2.Pin_1, Q2.B
  N5: LED1.cathode, R3.Pin_0
  N6: LED2.cathode, R4.Pin_0
  N7: R3.Pin_1, R4.Pin_1, Q2.C, Part3.GND

custom parts:
  Relay 5v DPDT: 5v DPDT Relay, 8 pin
  Adafruit Metro M0 Express: Metro is our series of microcontroller boards for use with the Arduino IDE. This new Metro board looks a whole lot like our original Metro 328, but with a huge upgrade. Instead of the ATmega328, this Metro features a ATSAMD21G18 chip, an ARM Cortex M0+. It's our first Metro that is designed for use with CircuitPython! CircuitPython is our beginner-oriented flavor of MicroPython - and as the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
