# Fritzing sketch CIRC13-express (saved by Fritzing 0.9.3b)
breadboards: 1

parts:
  J1 = Basic Force Sensing Resistor (FSR) [package=THT]
  R1 = Resistor [tolerance=±5% resistance=10k package=THT]
  LED2 = RGB LED - (4 legs) [package="5 mm [THT]"]
  R2 = Resistor [tolerance=±5% resistance=560 package=THT]
  R3 = Resistor [tolerance=±5% resistance=560 package=THT]
  R4 = Resistor [tolerance=±5% resistance=560 package=THT]
  Part3 = Adafruit Metro M0 Express

nets:
  N1: J1.pin_0, LED2.common_anode, Part3.3.3V
  N2: J1.pin_1, R1.Pin_1, Part3.A2
  N3: R1.Pin_0, Part3.GND
  N4: LED2.red_cathode, R2.Pin_1
  N5: LED2.green_cathode, R3.Pin_1
  N6: LED2.blue_cathode, R4.Pin_1
  N7: R2.Pin_0, Part3.D11
  N8: R3.Pin_0, Part3.D10
  N9: R4.Pin_0, Part3.D9

custom parts:
  Adafruit Metro M0 Express: Metro is our series of microcontroller boards for use with the Arduino IDE. This new Metro board looks a whole lot like our original Metro 328, but with a huge upgrade. Instead of the ATmega328, this Metro features a ATSAMD21G18 chip, an ARM Cortex M0+. It's our first Metro that is designed for use with CircuitPython! CircuitPython is our beginner-oriented flavor of MicroPython - and as the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
