# Fritzing sketch CIRC15-RGB-express (saved by Fritzing 0.9.3b)
breadboards: 1

parts:
  Part3 = Adafruit Metro M0 Express
  R1 = Resistor [tolerance=±5% resistance=560 package=THT]
  R2 = Resistor [tolerance=±5% resistance=560 package=THT]
  R3 = Resistor [tolerance=±5% resistance=560 package=THT]
  IR1 = TSOP312.., 314.. [package=THT]
  LED1 = RGB LED - (4 legs) [package="5 mm [THT]"]

nets:
  N1: Part3.D11, R3.Pin_0
  N2: Part3.D10, R1.Pin_0
  N3: Part3.D9, R2.Pin_0
  N4: Part3.D6, IR1.GND
  N5: Part3.3.3V, LED1.common_anode
  N6: Part3.GND, IR1.Vs
  N7: R1.Pin_1, LED1.green_cathode
  N8: R2.Pin_1, LED1.red_cathode
  N9: R3.Pin_1, LED1.blue_cathode

custom parts:
  Adafruit Metro M0 Express: Metro is our series of microcontroller boards for use with the Arduino IDE. This new Metro board looks a whole lot like our original Metro 328, but with a huge upgrade. Instead of the ATmega328, this Metro features a ATSAMD21G18 chip, an ARM Cortex M0+. It's our first Metro that is designed for use with CircuitPython! CircuitPython is our beginner-oriented flavor of MicroPython - and as the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
