# Fritzing sketch CIRC16-express (saved by Fritzing 0.9.3b)
breadboards: 1

parts:
  IR1 = TSOP312.., 314.. [package=THT]
  LED1 = Infrared LED - 5mm [package="5 mm [THT]"]  # not connected
  Q1 = NPN-Transistor [package="TO92 [THT]"]
  R1 = Resistor [tolerance=±5% resistance=560 package=THT]
  LED2 = LED - 5mm [color="Red (633nm)" package="5 mm [THT]"]
  R2 = Resistor [tolerance=±5% resistance=560 package=THT]
  S1 = Pushbutton [package="[THT]"]
  S2 = Pushbutton [package="[THT]"]
  R3 = Resistor [tolerance=±5% resistance=10k package=THT]
  R4 = Resistor [tolerance=±5% resistance=10k package=THT]
  Part3 = Adafruit Metro M0 Express

nets:
  N1: IR1.GND, Part3.D3
  N2: IR1.Vs, Q1.E, R2.Pin_0, Part3.GND
  N3: IR1.Data, S1.Pin_1, S1.Pin_2, S2.Pin_1, S2.Pin_2, R3.Pin_0, R4.Pin_0, Part3.3.3V
  N4: Q1.B, R1.Pin_1
  N5: R1.Pin_0, Part3.D9
  N6: LED2.cathode, R2.Pin_1
  N7: LED2.anode, Part3.D4
  N8: S1.Pin_3, S1.Pin_4, R3.Pin_1, Part3.D13
  N9: S2.Pin_3, S2.Pin_4, R4.Pin_1, Part3.D11

notes:
  REC
  PLAY

custom parts:
  Infrared LED - 5mm: A generic infrared LED (~1.2V)
  Adafruit Metro M0 Express: Metro is our series of microcontroller boards for use with the Arduino IDE. This new Metro board looks a whole lot like our original Metro 328, but with a huge upgrade. Instead of the ATmega328, this Metro features a ATSAMD21G18 chip, an ARM Cortex M0+. It's our first Metro that is designed for use with CircuitPython! CircuitPython is our beginner-oriented flavor of MicroPython - and as the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
