# Fritzing sketch CIRC16-mib-express (saved by Fritzing 0.9.3b)
breadboards: 1

parts:
  IR1 = TSOP312.., 314.. [package=THT]
  R2 = Resistor [tolerance=±5% resistance=560 package=THT]
  Part3 = Adafruit Metro M0 Express
  LED3 = RGB LED - (4 legs) [package="5 mm [THT]"]
  R3 = Resistor [tolerance=±5% resistance=560 package=THT]
  R4 = Resistor [tolerance=±5% resistance=560 package=THT]

nets:
  N1: IR1.GND, Part3.D6
  N2: IR1.Vs, Part3.GND
  N3: IR1.Data, Part3.3.3V, LED3.common_anode
  N4: R2.Pin_0, Part3.D12
  N5: R2.Pin_1, LED3.red_cathode
  N6: Part3.D10, R3.Pin_0
  N7: Part3.D9, R4.Pin_0
  N8: LED3.green_cathode, R3.Pin_1
  N9: LED3.blue_cathode, R4.Pin_1

custom parts:
  Adafruit Metro M0 Express: Metro is our series of microcontroller boards for use with the Arduino IDE. This new Metro board looks a whole lot like our original Metro 328, but with a huge upgrade. Instead of the ATmega328, this Metro features a ATSAMD21G18 chip, an ARM Cortex M0+. It's our first Metro that is designed for use with CircuitPython! CircuitPython is our beginner-oriented flavor of MicroPython - and as the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
