# Fritzing sketch CIRC18-express (saved by Fritzing 0.9.3b)
breadboards: 1

parts:
  Part3 = Adafruit Metro M0 Express
  POT1 = Breadboard Trimpot
  R1 = Resistor [tolerance=±5% resistance=10k package=THT]
  S1 = Tactile Switch Buttons - 12mm Square [package=tactile-pth-12mm]

nets:
  N1: Part3.A0, POT1.PIN2
  N2: Part3.D11, R1.Pin_1, S1.1, S1.3
  N3: Part3.3.3V, POT1.PIN1, R1.Pin_0
  N4: Part3.GND, POT1.PIN3, S1.2, S1.4

custom parts:
  Adafruit Metro M0 Express: Metro is our series of microcontroller boards for use with the Arduino IDE. This new Metro board looks a whole lot like our original Metro 328, but with a huge upgrade. Instead of the ATmega328, this Metro features a ATSAMD21G18 chip, an ARM Cortex M0+. It's our first Metro that is designed for use with CircuitPython! CircuitPython is our beginner-oriented flavor of MicroPython - and as the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
  Tactile Switch Buttons - 12mm Square: Medium-sized clicky momentary switches are standard input "buttons" on electronic projects. These work best in a PCB but can be used on a solderless breadboard as shown in this tutorial. The pins are normally open (disconnected) and when the button is pressed they are momentarily closed. They come in a pack of 10, they're pretty handy so you'll want to keep them around. You can find an EAGLE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
