# Fritzing sketch CIRC19-express (saved by Fritzing 0.9.3b)
breadboards: 1

parts:
  Part4 = Adafruit Metro M0 Express
  TRS1 = Audio Jack (TRS) 3.5mm [package="4Ucon 08780 [THT]"]
  POT1 = Breadboard Trimpot
  J1 = Basic Force Sensing Resistor (FSR) [package=THT]
  R1 = Resistor [tolerance=±5% resistance=10k package=THT]

nets:
  N1: Part4.A0, POT1.PIN2
  N2: Part4.A1, Part4.3.3V, J1.pin_0
  N3: Part4.GND, TRS1.Sleeve, POT1.PIN3, R1.Pin_0
  N4: TRS1.Ring, TRS1.Tip, POT1.PIN1
  N5: J1.pin_1, R1.Pin_1

custom parts:
  Adafruit Metro M0 Express: Metro is our series of microcontroller boards for use with the Arduino IDE. This new Metro board looks a whole lot like our original Metro 328, but with a huge upgrade. Instead of the ATmega328, this Metro features a ATSAMD21G18 chip, an ARM Cortex M0+. It's our first Metro that is designed for use with CircuitPython! CircuitPython is our beginner-oriented flavor of MicroPython - and as the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
