# Fritzing sketch PROJ01-express (saved by Fritzing 0.9.3b)
breadboards: 1

parts:
  J1 = Piezo Speaker
  Q1 = LTR-301 [package=ltr-301]
  R1 = Resistor [tolerance=±5% resistance=560 package=THT]
  Part5 = Adafruit Metro M0 Express

nets:
  N1: J1.pin1, Q1.C, Part5.GND
  N2: J1.pin2, Part5.D9
  N3: Q1.E, R1.Pin_1, Part5.A0
  N4: R1.Pin_0, Part5.+5V

custom parts:
  Adafruit Metro M0 Express: Metro is our series of microcontroller boards for use with the Arduino IDE. This new Metro board looks a whole lot like our original Metro 328, but with a huge upgrade. Instead of the ATmega328, this Metro features a ATSAMD21G18 chip, an ARM Cortex M0+. It's our first Metro that is designed for use with CircuitPython! CircuitPython is our beginner-oriented flavor of MicroPython - and as the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
