# Fritzing sketch PROJ02-express (saved by Fritzing 0.9.3b)
breadboards: 1

parts:
  LED24 = LED - 5mm [color="Green (555nm)" package="5 mm [THT]"]
  LED17 = LED - 5mm [color="Green (555nm)" package="5 mm [THT]"]
  LED18 = LED - 5mm [color="Green (555nm)" package="5 mm [THT]"]
  LED19 = LED - 5mm [color="Green (555nm)" package="5 mm [THT]"]
  LED20 = LED - 5mm [color="Green (555nm)" package="5 mm [THT]"]
  LED21 = LED - 5mm [color="Green (555nm)" package="5 mm [THT]"]
  LED22 = LED - 5mm [color="Green (555nm)" package="5 mm [THT]"]
  LED23 = LED - 5mm [color="Green (555nm)" package="5 mm [THT]"]
  R19 = Resistor [tolerance=±5% resistance=560 package=THT]
  R20 = Resistor [tolerance=±5% resistance=560 package=THT]
  R21 = Resistor [tolerance=±5% resistance=560 package=THT]
  R22 = Resistor [tolerance=±5% resistance=560 package=THT]
  R23 = Resistor [tolerance=±5% resistance=560 package=THT]
  R24 = Resistor [tolerance=±5% resistance=560 package=THT]
  R25 = Resistor [tolerance=±5% resistance=560 package=THT]
  R26 = Resistor [tolerance=±5% resistance=560 package=THT]
  VCC1 = Battery block 9V  # not connected
  JACK1 = 2.1mm DC Barrel Jack  # not connected
  Part2 = Adafruit Metro M0 Express

nets:
  N1: LED24.cathode, R24.Pin_0
  N2: LED24.anode, Part2.D4
  N3: LED17.cathode, R19.Pin_0
  N4: LED17.anode, Part2.D9
  N5: LED18.cathode, R25.Pin_0
  N6: LED18.anode, Part2.D3
  N7: LED19.cathode, R20.Pin_0
  N8: LED19.anode, Part2.D8
  N9: LED20.cathode, R21.Pin_0
  N10: LED20.anode, Part2.D7
  N11: LED21.cathode, R26.Pin_0
  N12: LED21.anode, Part2.D2
  N13: LED22.cathode, R22.Pin_0
  N14: LED22.anode, Part2.D6
  N15: LED23.cathode, R23.Pin_0
  N16: LED23.anode, Part2.D5
  N17: R19.Pin_1, R20.Pin_1, R21.Pin_1, R22.Pin_1, R23.Pin_1, R24.Pin_1, R25.Pin_1, R26.Pin_1, Part2.GND

custom parts:
  2.1mm DC Barrel Jack: 2.1mm DC Barrel Jack with Thru-Hole Connectors (breadboardable)
  Adafruit Metro M0 Express: Metro is our series of microcontroller boards for use with the Arduino IDE. This new Metro board looks a whole lot like our original Metro 328, but with a huge upgrade. Instead of the ATmega328, this Metro features a ATSAMD21G18 chip, an ARM Cortex M0+. It's our first Metro that is designed for use with CircuitPython! CircuitPython is our beginner-oriented flavor of MicroPython - and as the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
