# Fritzing sketch PROJ03-express (saved by Fritzing 0.9.3b)
breadboards: 1

parts:
  U1 = LCD-16X2 [package=lcd-16x2_noholes]
  POT1 = Breadboard Trimpot
  Q1 = LTR-301 [package=ltr-301]
  R1 = Resistor [tolerance=±5% resistance=10k package=THT]
  J1 = Piezo Speaker
  Part3 = Adafruit Metro M0 Express

nets:
  VSS: U1.VSS, U1.R_W, U1.K, POT1.PIN1, Q1.C, J1.pin1, Part3.GND
  VDD: U1.VDD, U1.A, POT1.PIN3, R1.Pin_0, Part3.3.3V
  N1: U1.VO, POT1.PIN2
  N2: U1.RS, Part3.D7
  N3: U1.E, Part3.D8
  N4: U1.DB4, Part3.D9
  N5: U1.DB5, Part3.D10
  N6: U1.DB6, Part3.D11
  N7: U1.DB7, Part3.D12
  N8: Q1.E, R1.Pin_1, Part3.A0
  N9: J1.pin2, Part3.D13

custom parts:
  Adafruit Metro M0 Express: Metro is our series of microcontroller boards for use with the Arduino IDE. This new Metro board looks a whole lot like our original Metro 328, but with a huge upgrade. Instead of the ATmega328, this Metro features a ATSAMD21G18 chip, an ARM Cortex M0+. It's our first Metro that is designed for use with CircuitPython! CircuitPython is our beginner-oriented flavor of MicroPython - and as the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
